# Fritzing sketch Arduino_connection (saved by Fritzing 0.9.3b)
breadboards: 1

parts:
  Part2 = RFM9xW
  Part3 = Arduino Pro Mini v13
  Part4 = FTDI Basic Programmer
  RHT1 = Humidity and Temperature Sensor RHT03

nets:
  N1: Part2.MOSI, Part3.D11_PWM/MOSI
  N2: Part2.SCK, Part3.D13/SCK
  N3: Part2.NSS, Part3.D6_PWM
  N4: Part2.RESET, Part3.D5_PWM
  GND: Part2.GND#7, Part2.GND#9, Part3.GND, Part4.CTS, Part4.GND, RHT1.GND_2
  VCC: Part2.VCC, Part3.VCC, Part4.POWER, RHT1.Vcc
  N5: Part2.DIO0, Part3.D2
  N6: Part2.DIO1, Part3.D3_PWM
  N7: Part2.DIO2, Part3.D4
  N8: Part3.DTR, Part4.DTR
  N9: Part3.D0/TX, Part4.RXI
  N10: Part3.D1/RX, Part4.TXO
  N11: Part3.D10_PWM/SS, RHT1.Data-signal

notes:
  3v3 Arduino
  3v3 FTDI
  https://goo.gl/sdp3Rb
  MORA LoRaWan

custom parts:
  RFM9xW: RFM9xW Module connector
